// Logisim project controller.circ as structural Verilog: 1 circuit, main circuit main
module main (
);

  wire and_1_out, and_2_out, and_3_out, and_4_out, and_5_out, and_6_out, and_7_out, and_8_out, and_9_out,
       and_10_out, and_11_out, and_12_out, and_13_out, and_14_out, and_15_out, and_16_out, and_17_out,
       and_18_out, and_19_out, and_20_out, clock_1_out, d_ff_1_qn, dipswitch_1_p1, dipswitch_1_p2,
       dipswitch_1_p3, dipswitch_1_p4, dipswitch_1_p5, dipswitch_1_p6, dipswitch_1_p7, dipswitch_1_p8,
       nor_1_out, not_1_out, not_2_out, not_3_out, not_4_out, not_5_out, not_6_out, not_7_out, not_8_out,
       not_9_out, not_10_out, not_11_out, not_12_out, not_13_out, not_14_out, not_15_out, not_16_out,
       not_17_out, not_18_out, not_19_out, not_20_out, not_21_out, not_22_out, not_23_out, not_24_out,
       not_25_out, not_26_out, not_27_out, or_1_out, or_2_out;
  wire [4:0] counter_1_q;

  Clock clock_1 (.out(clock_1_out));
  D_Flip_Flop d_ff_1 (.clk(clock_1_out), .D(counter_1_q[0]), .Qn(d_ff_1_qn));  // open: Q, preset, reset
  Counter #(.width(5), .max('h1f)) counter_1 (
    .count(d_ff_1_qn), .Q(counter_1_q), .clk(clock_1_out), .clr(and_1_out));  // open: load, D, carry, preset, down
  not not_1 (not_1_out, counter_1_q[0]);
  not not_2 (not_2_out, counter_1_q[2]);
  not not_3 (not_3_out, counter_1_q[3]);
  and and_1 (and_1_out, counter_1_q[4], not_3_out, not_2_out, counter_1_q[1], not_1_out);
  not not_4 (not_4_out, counter_1_q[4]);
  not not_5 (not_5_out, counter_1_q[3]);
  and and_2 (and_2_out, not_4_out, not_5_out, not_6_out, not_9_out);
  // DipSwitch #(.NSwitches(8)) dipswitch_1: pin names not known; wires that end beside it: dipswitch_1_p1, dipswitch_1_p2, dipswitch_1_p3, dipswitch_1_p4, dipswitch_1_p5, dipswitch_1_p6, dipswitch_1_p7, dipswitch_1_p8
  nor nor_1 (nor_1_out, counter_1_q[0], d_ff_1_qn);
  not not_6 (not_6_out, counter_1_q[2]);
  not not_7 (not_7_out, counter_1_q[2]);
  not not_8 (not_8_out, counter_1_q[4]);
  not not_9 (not_9_out, counter_1_q[1]);
  not not_10 (not_10_out, counter_1_q[3]);
  and and_3 (and_3_out, not_8_out, not_10_out, not_7_out, counter_1_q[1]);
  and and_4 (and_4_out, and_3_out, dipswitch_1_p2);
  and and_5 (and_5_out, and_2_out, dipswitch_1_p1);
  not not_11 (not_11_out, counter_1_q[4]);
  not not_12 (not_12_out, counter_1_q[3]);
  not not_13 (not_13_out, counter_1_q[1]);
  not not_14 (not_14_out, counter_1_q[4]);
  and and_6 (and_6_out, not_14_out, not_12_out, counter_1_q[2], not_13_out);
  and and_7 (and_7_out, and_6_out, dipswitch_1_p3);
  not not_15 (not_15_out, counter_1_q[4]);
  not not_16 (not_16_out, counter_1_q[3]);
  and and_8 (and_8_out, not_11_out, not_16_out, counter_1_q[2], counter_1_q[1]);
  and and_9 (and_9_out, not_15_out, counter_1_q[3], not_20_out, not_21_out);
  and and_10 (and_10_out, and_8_out, dipswitch_1_p4);
  or or_1 (or_1_out, and_5_out, and_4_out, and_7_out, and_10_out, and_14_out, and_13_out, and_16_out, and_19_out);
  not not_17 (not_17_out, counter_1_q[0]);
  and and_11 (and_11_out, not_17_out, or_1_out);
  LED led_1 (.in(or_2_out));
  or or_2 (or_2_out, nor_1_out, and_11_out, and_20_out);
  not not_18 (not_18_out, counter_1_q[4]);
  not not_19 (not_19_out, counter_1_q[2]);
  not not_20 (not_20_out, counter_1_q[2]);
  not not_21 (not_21_out, counter_1_q[1]);
  and and_12 (and_12_out, not_18_out, counter_1_q[3], not_19_out, counter_1_q[1]);
  and and_13 (and_13_out, and_12_out, dipswitch_1_p6);
  and and_14 (and_14_out, and_9_out, dipswitch_1_p5);
  not not_22 (not_22_out, counter_1_q[4]);
  not not_23 (not_23_out, counter_1_q[4]);
  not not_24 (not_24_out, counter_1_q[1]);
  and and_15 (and_15_out, not_23_out, counter_1_q[3], counter_1_q[2], not_24_out);
  and and_16 (and_16_out, and_15_out, dipswitch_1_p7);
  not not_25 (not_25_out, counter_1_q[3]);
  and and_17 (and_17_out, counter_1_q[4], not_25_out, not_27_out, not_26_out);
  and and_18 (and_18_out, not_22_out, counter_1_q[3], counter_1_q[2], counter_1_q[1]);
  and and_19 (and_19_out, and_18_out, dipswitch_1_p8);
  not not_26 (not_26_out, counter_1_q[1]);
  not not_27 (not_27_out, counter_1_q[2]);
  and and_20 (and_20_out, and_17_out, 1'b1);
endmodule
